// Logisim project ALU.circ as structural Verilog: 12 circuits, main circuit main
module main (
  input  [1:0] in_1,
  input  [7:0] in_2,
  input  [7:0] in_3,
  output [7:0] out_4,
  output out_5
);

  wire and_1_out, and_2_out, and_3_out, n8_bit_adder_1_out_4, n8_bit_multiplier_1_out_4, nor_1_out,
       not_1_out, not_2_out;
  wire [7:0] n8_bit_adder_1_out_3, n8_bit_divider_1_out_3, n8_bit_multiplier_1_out_3,
       n8_bit_subtractor_1_out_3, n8_by_1_bit_multiplier_1_out_3, n8_by_1_bit_multiplier_2_out_3,
       n8_by_1_bit_multiplier_3_out_3, n8_by_1_bit_multiplier_4_out_3, n8_by_1_bit_multiplier_5_out_3,
       n8_by_1_bit_multiplier_6_out_3, n8_by_1_bit_multiplier_7_out_3, n8_by_1_bit_multiplier_8_out_3;

  not not_1 (not_1_out, in_1[1]);
  not not_2 (not_2_out, in_1[0]);
  nor nor_1 (nor_1_out, in_1[0], in_1[1]);
  and and_1 (and_1_out, in_1[0], not_1_out);
  and and_2 (and_2_out, not_2_out, in_1[0]);
  and and_3 (and_3_out, in_1[0], in_1[1]);
  _8_by_1_Bit_Multiplier u_8_by_1_bit_multiplier_1 (
    .in_1(nor_1_out), .in_2(in_2), .out_3(n8_by_1_bit_multiplier_1_out_3));
  _8_by_1_Bit_Multiplier u_8_by_1_bit_multiplier_2 (
    .in_1(nor_1_out), .in_2(in_3), .out_3(n8_by_1_bit_multiplier_2_out_3));
  _8_by_1_Bit_Multiplier u_8_by_1_bit_multiplier_3 (
    .in_1(and_1_out), .in_2(in_2), .out_3(n8_by_1_bit_multiplier_3_out_3));
  _8_by_1_Bit_Multiplier u_8_by_1_bit_multiplier_4 (
    .in_1(and_1_out), .in_2(in_3), .out_3(n8_by_1_bit_multiplier_4_out_3));
  _8_by_1_Bit_Multiplier u_8_by_1_bit_multiplier_5 (
    .in_1(and_2_out), .in_2(in_2), .out_3(n8_by_1_bit_multiplier_5_out_3));
  _8_by_1_Bit_Multiplier u_8_by_1_bit_multiplier_6 (
    .in_1(and_2_out), .in_2(in_3), .out_3(n8_by_1_bit_multiplier_6_out_3));
  _8_by_1_Bit_Multiplier u_8_by_1_bit_multiplier_7 (
    .in_1(and_3_out), .in_2(in_2), .out_3(n8_by_1_bit_multiplier_7_out_3));
  _8_by_1_Bit_Multiplier u_8_by_1_bit_multiplier_8 (
    .in_1(and_3_out), .in_2(in_3), .out_3(n8_by_1_bit_multiplier_8_out_3));
  _8_Bit_Adder u_8_bit_adder_1 (
    .in_1(n8_by_1_bit_multiplier_1_out_3), .in_2(n8_by_1_bit_multiplier_2_out_3),
    .out_3(n8_bit_adder_1_out_3), .out_4(n8_bit_adder_1_out_4));
  _8_Bit_Subtractor u_8_bit_subtractor_1 (
    .in_1(n8_by_1_bit_multiplier_3_out_3), .in_2(n8_by_1_bit_multiplier_4_out_3),
    .out_3(n8_bit_subtractor_1_out_3));
  _8_Bit_Multiplier u_8_bit_multiplier_1 (
    .in_1(n8_by_1_bit_multiplier_5_out_3), .in_2(n8_by_1_bit_multiplier_6_out_3),
    .out_3(n8_bit_multiplier_1_out_3), .out_4(n8_bit_multiplier_1_out_4));
  _8_Bit_Divider u_8_bit_divider_1 (
    .in_1(n8_by_1_bit_multiplier_7_out_3), .in_2(n8_by_1_bit_multiplier_8_out_3),
    .out_3(n8_bit_divider_1_out_3));
  or or_1 (out_5, n8_bit_adder_1_out_4, n8_bit_multiplier_1_out_4);
  assign out_4 = n8_bit_adder_1_out_3 | n8_bit_subtractor_1_out_3 | n8_bit_multiplier_1_out_3 | n8_bit_divider_1_out_3;  // OR_Gate or_2, 8 bits wide
endmodule

// HA
module Half_Adder (
  input  in_1,
  input  in_2,
  output Sum,
  output Carry
);

  wire not_1_out, or_1_out;

  or or_1 (or_1_out, in_1, in_2);
  not not_1 (not_1_out, Carry);
  and and_1 (Carry, in_1, in_2);
  and and_2 (Sum, or_1_out, not_1_out);
endmodule

// FA
module Full_Adder (
  input  in_1,
  input  in_2,
  input  in_3,
  output out_4,
  output out_5
);

  wire half_adder_1_carry, half_adder_1_sum, half_adder_2_carry;

  Half_Adder half_adder_1 (.in_1(in_1), .in_2(in_2), .Sum(half_adder_1_sum), .Carry(half_adder_1_carry));
  Half_Adder half_adder_2 (.in_1(half_adder_1_sum), .in_2(in_3), .Sum(out_4), .Carry(half_adder_2_carry));
  or or_1 (out_5, half_adder_1_carry, half_adder_2_carry);
endmodule

// Add
module _8_Bit_Adder (
  input  [7:0] in_1,
  input  [7:0] in_2,
  output [7:0] out_3,
  output out_4
);

  General_Adder general_adder_1 (.in_1(1'b0), .in_2(in_1), .in_3(in_2), .out_4(out_3), .out_5(out_4));
endmodule

// Sub
module _8_Bit_Subtractor (
  input  [7:0] in_1,
  input  [7:0] in_2,
  output [7:0] out_3
);

  wire [7:0] not_1_out;

  assign not_1_out = ~in_2;  // NOT_Gate not_1, 8 bits wide
  General_Adder general_adder_1 (.in_1(1'b1), .in_2(in_1), .in_3(not_1_out), .out_4(out_3));  // open: out_5
endmodule

// Mult
module _8_by_1_Bit_Multiplier (
  input  in_1,
  input  [7:0] in_2,
  output [7:0] out_3
);

  and and_1 (out_3[0], in_2[0], in_1);
  and and_2 (out_3[1], in_2[1], in_1);
  and and_3 (out_3[2], in_2[2], in_1);
  and and_4 (out_3[3], in_2[3], in_1);
  and and_5 (out_3[4], in_2[4], in_1);
  and and_6 (out_3[5], in_2[5], in_1);
  and and_7 (out_3[6], in_2[6], in_1);
  and and_8 (out_3[7], in_2[7], in_1);
endmodule

// Mul
module _8_Bit_Multiplier (
  input  [7:0] in_1,
  input  [7:0] in_2,
  output [7:0] out_3,
  output out_4
);

  wire [7:0] n8_bit_adder_1_out_3, n8_bit_adder_2_out_3, n8_bit_adder_3_out_3, n8_bit_adder_4_out_3,
       n8_bit_adder_5_out_3, n8_bit_adder_6_out_3, n8_by_1_bit_multiplier_1_out_3,
       n8_by_1_bit_multiplier_2_out_3, n8_by_1_bit_multiplier_3_out_3, n8_by_1_bit_multiplier_4_out_3,
       n8_by_1_bit_multiplier_5_out_3, n8_by_1_bit_multiplier_6_out_3, n8_by_1_bit_multiplier_7_out_3,
       n8_by_1_bit_multiplier_8_out_3, shifter_1_out, shifter_2_out, shifter_3_out, shifter_4_out,
       shifter_5_out, shifter_6_out, shifter_7_out;

  _8_by_1_Bit_Multiplier u_8_by_1_bit_multiplier_1 (
    .in_1(in_2[0]), .in_2(in_1), .out_3(n8_by_1_bit_multiplier_1_out_3));
  _8_by_1_Bit_Multiplier u_8_by_1_bit_multiplier_2 (
    .in_1(in_2[1]), .in_2(in_1), .out_3(n8_by_1_bit_multiplier_2_out_3));
  _8_by_1_Bit_Multiplier u_8_by_1_bit_multiplier_3 (
    .in_1(in_2[2]), .in_2(in_1), .out_3(n8_by_1_bit_multiplier_3_out_3));
  _8_by_1_Bit_Multiplier u_8_by_1_bit_multiplier_4 (
    .in_1(in_2[3]), .in_2(in_1), .out_3(n8_by_1_bit_multiplier_4_out_3));
  _8_by_1_Bit_Multiplier u_8_by_1_bit_multiplier_5 (
    .in_1(in_2[4]), .in_2(in_1), .out_3(n8_by_1_bit_multiplier_5_out_3));
  _8_by_1_Bit_Multiplier u_8_by_1_bit_multiplier_6 (
    .in_1(in_2[5]), .in_2(in_1), .out_3(n8_by_1_bit_multiplier_6_out_3));
  _8_by_1_Bit_Multiplier u_8_by_1_bit_multiplier_7 (
    .in_1(in_2[6]), .in_2(in_1), .out_3(n8_by_1_bit_multiplier_7_out_3));
  _8_by_1_Bit_Multiplier u_8_by_1_bit_multiplier_8 (
    .in_1(in_2[7]), .in_2(in_1), .out_3(n8_by_1_bit_multiplier_8_out_3));
  Shifter shifter_1 (.in(n8_by_1_bit_multiplier_2_out_3), .\dist (3'b001), .out(shifter_1_out));
  Shifter shifter_2 (.in(n8_by_1_bit_multiplier_3_out_3), .\dist (3'b010), .out(shifter_2_out));
  Shifter shifter_3 (.in(n8_by_1_bit_multiplier_4_out_3), .\dist (3'b011), .out(shifter_3_out));
  Shifter shifter_4 (.in(n8_by_1_bit_multiplier_5_out_3), .\dist (3'b100), .out(shifter_4_out));
  Shifter shifter_5 (.in(n8_by_1_bit_multiplier_6_out_3), .\dist (3'b101), .out(shifter_5_out));
  Shifter shifter_6 (.in(n8_by_1_bit_multiplier_7_out_3), .\dist (3'b110), .out(shifter_6_out));
  Shifter shifter_7 (.in(n8_by_1_bit_multiplier_8_out_3), .\dist (3'b111), .out(shifter_7_out));
  _8_Bit_Adder u_8_bit_adder_1 (
    .in_1(n8_by_1_bit_multiplier_1_out_3), .in_2(shifter_1_out), .out_3(n8_bit_adder_1_out_3));  // open: out_4
  _8_Bit_Adder u_8_bit_adder_2 (
    .in_1(n8_bit_adder_1_out_3), .in_2(shifter_2_out), .out_3(n8_bit_adder_2_out_3));  // open: out_4
  _8_Bit_Adder u_8_bit_adder_3 (
    .in_1(n8_bit_adder_2_out_3), .in_2(shifter_3_out), .out_3(n8_bit_adder_3_out_3));  // open: out_4
  _8_Bit_Adder u_8_bit_adder_4 (
    .in_1(n8_bit_adder_3_out_3), .in_2(shifter_4_out), .out_3(n8_bit_adder_4_out_3));  // open: out_4
  _8_Bit_Adder u_8_bit_adder_5 (
    .in_1(n8_bit_adder_4_out_3), .in_2(shifter_5_out), .out_3(n8_bit_adder_5_out_3));  // open: out_4
  _8_Bit_Adder u_8_bit_adder_6 (
    .in_1(n8_bit_adder_5_out_3), .in_2(shifter_6_out), .out_3(n8_bit_adder_6_out_3));  // open: out_4
  _8_Bit_Adder u_8_bit_adder_7 (.in_1(n8_bit_adder_6_out_3), .in_2(shifter_7_out), .out_3(out_3), .out_4(out_4));
endmodule

// GA
module General_Adder (
  input  in_1,
  input  [7:0] in_2,
  input  [7:0] in_3,
  output [7:0] out_4,
  output out_5
);

  wire full_adder_1_out_5, full_adder_2_out_5, full_adder_3_out_5, full_adder_4_out_5, full_adder_5_out_5,
       full_adder_6_out_5, full_adder_7_out_5;

  Full_Adder full_adder_1 (.in_1(in_1), .in_2(in_2[0]), .in_3(in_3[0]), .out_4(out_4[0]), .out_5(full_adder_1_out_5));
  Full_Adder full_adder_2 (
    .in_1(full_adder_1_out_5), .in_2(in_2[1]), .in_3(in_3[1]), .out_4(out_4[1]), .out_5(full_adder_2_out_5));
  Full_Adder full_adder_3 (
    .in_1(full_adder_2_out_5), .in_2(in_2[2]), .in_3(in_3[2]), .out_4(out_4[2]), .out_5(full_adder_3_out_5));
  Full_Adder full_adder_4 (
    .in_1(full_adder_3_out_5), .in_2(in_2[3]), .in_3(in_3[3]), .out_4(out_4[3]), .out_5(full_adder_4_out_5));
  Full_Adder full_adder_5 (
    .in_1(full_adder_4_out_5), .in_2(in_2[4]), .in_3(in_3[4]), .out_4(out_4[4]), .out_5(full_adder_5_out_5));
  Full_Adder full_adder_6 (
    .in_1(full_adder_5_out_5), .in_2(in_2[5]), .in_3(in_3[5]), .out_4(out_4[5]), .out_5(full_adder_6_out_5));
  Full_Adder full_adder_7 (
    .in_1(full_adder_6_out_5), .in_2(in_2[6]), .in_3(in_3[6]), .out_4(out_4[6]), .out_5(full_adder_7_out_5));
  Full_Adder full_adder_8 (.in_1(full_adder_7_out_5), .in_2(in_2[7]), .in_3(in_3[7]), .out_4(out_4[7]), .out_5(out_5));
endmodule

// Div
module _8_Bit_Divider (
  input  [7:0] in_1,
  input  [7:0] in_2,
  output [7:0] out_3
);

  wire or_1_out, over_shift_1_out_4, over_shift_2_out_4, over_shift_3_out_4, over_shift_4_out_4,
       over_shift_5_out_4, over_shift_6_out_4, over_shift_7_out_4, positive_sub_1_out_3,
       positive_sub_2_out_3, positive_sub_3_out_3, positive_sub_4_out_3, positive_sub_5_out_3,
       positive_sub_6_out_3, positive_sub_7_out_3, positive_sub_8_out_3;
  wire [7:0] not_1_out, over_shift_1_out_3, over_shift_2_out_3, over_shift_3_out_3, over_shift_4_out_3,
       over_shift_5_out_3, over_shift_6_out_3, over_shift_7_out_3, positive_sub_1_out_4,
       positive_sub_2_out_4, positive_sub_3_out_4, positive_sub_4_out_4, positive_sub_5_out_4,
       positive_sub_6_out_4, positive_sub_7_out_4;

  Over_Shift over_shift_1 (.in_1(in_2), .in_2(3'b111), .out_3(over_shift_1_out_3), .out_4(over_shift_1_out_4));
  Positive_Sub positive_sub_1 (
    .in_1(in_1), .in_2(over_shift_1_out_3), .out_3(positive_sub_1_out_3), .out_4(positive_sub_1_out_4));
  Positive_Sub positive_sub_2 (
    .in_1(positive_sub_1_out_4), .in_2(over_shift_2_out_3), .out_3(positive_sub_2_out_3),
    .out_4(positive_sub_2_out_4));
  Over_Shift over_shift_2 (.in_1(in_2), .in_2(3'b110), .out_3(over_shift_2_out_3), .out_4(over_shift_2_out_4));
  nor nor_1 (not_1_out[7], over_shift_1_out_4, positive_sub_1_out_3);
  nor nor_2 (not_1_out[6], over_shift_2_out_4, positive_sub_2_out_3);
  Positive_Sub positive_sub_3 (
    .in_1(positive_sub_2_out_4), .in_2(over_shift_3_out_3), .out_3(positive_sub_3_out_3),
    .out_4(positive_sub_3_out_4));
  Over_Shift over_shift_3 (.in_1(in_2), .in_2(3'b101), .out_3(over_shift_3_out_3), .out_4(over_shift_3_out_4));
  nor nor_3 (not_1_out[5], over_shift_3_out_4, positive_sub_3_out_3);
  Positive_Sub positive_sub_4 (
    .in_1(positive_sub_3_out_4), .in_2(over_shift_4_out_3), .out_3(positive_sub_4_out_3),
    .out_4(positive_sub_4_out_4));
  Over_Shift over_shift_4 (.in_1(in_2), .in_2(3'b100), .out_3(over_shift_4_out_3), .out_4(over_shift_4_out_4));
  Over_Shift over_shift_5 (.in_1(in_2), .in_2(3'b011), .out_3(over_shift_5_out_3), .out_4(over_shift_5_out_4));
  nor nor_4 (not_1_out[4], over_shift_4_out_4, positive_sub_4_out_3);
  Positive_Sub positive_sub_5 (
    .in_1(positive_sub_4_out_4), .in_2(over_shift_5_out_3), .out_3(positive_sub_5_out_3),
    .out_4(positive_sub_5_out_4));
  Over_Shift over_shift_6 (.in_1(in_2), .in_2(3'b010), .out_3(over_shift_6_out_3), .out_4(over_shift_6_out_4));
  nor nor_5 (not_1_out[3], over_shift_5_out_4, positive_sub_5_out_3);
  Positive_Sub positive_sub_6 (
    .in_1(positive_sub_5_out_4), .in_2(over_shift_6_out_3), .out_3(positive_sub_6_out_3),
    .out_4(positive_sub_6_out_4));
  Over_Shift over_shift_7 (.in_1(in_2), .in_2(3'b001), .out_3(over_shift_7_out_3), .out_4(over_shift_7_out_4));
  nor nor_6 (not_1_out[2], over_shift_6_out_4, positive_sub_6_out_3);
  Positive_Sub positive_sub_7 (
    .in_1(positive_sub_6_out_4), .in_2(over_shift_7_out_3), .out_3(positive_sub_7_out_3),
    .out_4(positive_sub_7_out_4));
  nor nor_7 (not_1_out[1], over_shift_7_out_4, positive_sub_7_out_3);
  Positive_Sub positive_sub_8 (.in_1(positive_sub_7_out_4), .in_2(in_2), .out_3(positive_sub_8_out_3));  // open: out_4
  not not_1 (not_1_out[0], positive_sub_8_out_3);
  or or_1 (or_1_out, in_2[0], in_2[1], in_2[2], in_2[3], in_2[4], in_2[5], in_2[6], in_2[7]);
  _8_by_1_Bit_Multiplier u_8_by_1_bit_multiplier_1 (.in_1(or_1_out), .in_2(not_1_out), .out_3(out_3));
endmodule

// PS
module Positive_Sub (
  input  [7:0] in_1,
  input  [7:0] in_2,
  output out_3,
  output [7:0] out_4
);

  wire not_2_out;
  wire [6:0] general_adder_1_out_4;
  wire [7:0] n8_by_1_bit_multiplier_1_out_3, n8_by_1_bit_multiplier_2_out_3, not_1_out;

  assign not_1_out = ~in_2;  // NOT_Gate not_1, 8 bits wide
  General_Adder general_adder_1 (
    .in_1(1'b1), .in_2(in_1), .in_3(not_1_out), .out_4({out_3, general_adder_1_out_4}));  // open: out_5
  _8_by_1_Bit_Multiplier u_8_by_1_bit_multiplier_1 (.in_1(out_3), .in_2(in_1), .out_3(n8_by_1_bit_multiplier_1_out_3));
  not not_2 (not_2_out, out_3);
  _8_by_1_Bit_Multiplier u_8_by_1_bit_multiplier_2 (
    .in_1(not_2_out), .in_2({out_3, general_adder_1_out_4}), .out_3(n8_by_1_bit_multiplier_2_out_3));
  _8_Bit_Adder u_8_bit_adder_1 (
    .in_1(n8_by_1_bit_multiplier_1_out_3), .in_2(n8_by_1_bit_multiplier_2_out_3), .out_3(out_4));  // open: out_4
endmodule

// OS
module Over_Shift (
  input  [7:0] in_1,
  input  [2:0] in_2,
  output [7:0] out_3,
  output out_4
);

  wire or_1_out;

  Shifter shifter_1 (.in(in_1), .\dist (in_2), .out(out_3));
  or or_1 (or_1_out, out_3[0], out_3[1], out_3[2], out_3[3], out_3[4], out_3[5], out_3[6], out_3[7]);
  not not_1 (out_4, or_1_out);
endmodule

// Mod
module _8_Bit_Modulo (
  input  [7:0] in_1,
  input  [7:0] in_2,
  output [7:0] out_3
);

  wire [7:0] over_shift_1_out_3, over_shift_2_out_3, over_shift_3_out_3, over_shift_4_out_3,
       over_shift_5_out_3, over_shift_6_out_3, over_shift_7_out_3, positive_sub_1_out_4,
       positive_sub_2_out_4, positive_sub_3_out_4, positive_sub_4_out_4, positive_sub_5_out_4,
       positive_sub_6_out_4, positive_sub_7_out_4;

  Over_Shift over_shift_1 (.in_1(in_2), .in_2(3'b111), .out_3(over_shift_1_out_3));  // open: out_4
  Positive_Sub positive_sub_1 (.in_1(in_1), .in_2(over_shift_1_out_3), .out_4(positive_sub_1_out_4));  // open: out_3
  Over_Shift over_shift_2 (.in_1(in_2), .in_2(3'b110), .out_3(over_shift_2_out_3));  // open: out_4
  Positive_Sub positive_sub_2 (
    .in_1(positive_sub_1_out_4), .in_2(over_shift_2_out_3), .out_4(positive_sub_2_out_4));  // open: out_3
  Over_Shift over_shift_3 (.in_1(in_2), .in_2(3'b101), .out_3(over_shift_3_out_3));  // open: out_4
  Positive_Sub positive_sub_3 (
    .in_1(positive_sub_2_out_4), .in_2(over_shift_3_out_3), .out_4(positive_sub_3_out_4));  // open: out_3
  Positive_Sub positive_sub_4 (
    .in_1(positive_sub_3_out_4), .in_2(over_shift_4_out_3), .out_4(positive_sub_4_out_4));  // open: out_3
  Over_Shift over_shift_4 (.in_1(in_2), .in_2(3'b100), .out_3(over_shift_4_out_3));  // open: out_4
  Positive_Sub positive_sub_5 (
    .in_1(positive_sub_4_out_4), .in_2(over_shift_5_out_3), .out_4(positive_sub_5_out_4));  // open: out_3
  Over_Shift over_shift_5 (.in_1(in_2), .in_2(3'b011), .out_3(over_shift_5_out_3));  // open: out_4
  Positive_Sub positive_sub_6 (
    .in_1(positive_sub_5_out_4), .in_2(over_shift_6_out_3), .out_4(positive_sub_6_out_4));  // open: out_3
  Over_Shift over_shift_6 (.in_1(in_2), .in_2(3'b010), .out_3(over_shift_6_out_3));  // open: out_4
  Over_Shift over_shift_7 (.in_1(in_2), .in_2(3'b001), .out_3(over_shift_7_out_3));  // open: out_4
  Positive_Sub positive_sub_7 (
    .in_1(positive_sub_6_out_4), .in_2(over_shift_7_out_3), .out_4(positive_sub_7_out_4));  // open: out_3
  Positive_Sub positive_sub_8 (.in_1(positive_sub_7_out_4), .in_2(in_2), .out_4(out_3));  // open: out_3
endmodule
